# Fritzing sketch rise_and_shine_circuit_rotary_encoder_v0_1 (saved by Fritzing 0.9.2b)
breadboards: 1

parts:
  S2 = Pushbutton [package="[THT]"]
  Part2 = Real Time Clock Module - DS1307 RTC Breakout Board
  Power_plug1 = Power plug
  Part1 = Arduino Nano (Rev3.0)
  RE1 = Rotary Encoder [package=THT]
  RGB_SMD_LED1 = SMD RGB LED (WS2812) [package=5050]

nets:
  N1: S2.Pin_1, S2.Pin_2, Part1.A3
  GND: S2.Pin_3, S2.Pin_4, Part2.GND, Power_plug1.GND, Part1.GND, RE1.EncoderPinC, RGB_SMD_LED1.VSS
  5V: Part2.5V, Power_plug1.VCC, Part1.5V, RGB_SMD_LED1.VCC
  N2: Part2.SCL, Part1.A5
  N3: Part2.SDA, Part1.A4
  N4: Part1.D2, RE1.EncoderPinB
  N5: Part1.D3, RE1.EncoderPinA
  N6: Part1.A0, RGB_SMD_LED1.DIn
